// Logisim project cpu.circ as structural Verilog: 1 circuit, main circuit main
module main (
  input  [31:0] RS_READ_VALUE,
  input  [31:0] RT_READ_VALUE,
  input  [31:0] INSTRUCTION,
  input  CLOCK,
  input  RESET,
  output [31:0] t0,
  output [31:0] t1,
  output [31:0] t2,
  output [31:0] t3,
  output [4:0] RS,
  output [4:0] RT,
  output [4:0] Write_Register,
  output [31:0] RD_WRITE_VALUE,
  output RD_WRITE_ENABLE,
  output [23:0] FETCH_ADDRESS
);

  wire ALU_signed_overflow, pc_1_or_naw;
  wire [23:0] Incremented, jump_address, multiplexer_1_out;
  wire [31:0] bit_extender_1_out, multiplexer_2_out;

  Adder #(.width(24)) adder_1 (.a(FETCH_ADDRESS), .b(24'h1), .out(Incremented));  // open: cin, cout
  Multiplexer #(.width(24)) multiplexer_1 (
    .in0(Incremented), .in1(jump_address), .out(multiplexer_1_out), .sel(pc_1_or_naw));  // open: en
  Multiplexer #(.width(32)) multiplexer_2 (
    .in0(RT_READ_VALUE), .in1(bit_extender_1_out), .out(multiplexer_2_out));  // open: sel, en
  assign bit_extender_1_out = {{16{1'b0}}, INSTRUCTION[15:0]};  // Bit_Extender bit_extender_1
  alu_main ALU (
    .Switch__S(INSTRUCTION[31:26]), .X(RS_READ_VALUE), .Signed_Overflow(ALU_signed_overflow),
    .Y(multiplexer_2_out));  // open: Equal, RESULT
  Register #(.width(24)) register_1 (.D(multiplexer_1_out), .Q(FETCH_ADDRESS), .clk(CLOCK));  // open: en, clr
  LED led_1 (.in(ALU_signed_overflow));
  mem_main MEM (.CLOCK(CLOCK));  // open: Data_Mem_Addr, Data_Mem_In, ACCESS_BYTE, MEM_WRITE, Data_Mem_Out
  regfile_main RegFile (
    .t0_Value(t0), .t1_Value(t1), .t2_Value(t2), .t3_Value(t3), .clock(CLOCK));  // open: Read_register_1, Read_register_2, write_register, write_data, RegWrite, Read_Data_1, Read_Data_2

  // Other names for the same wires on the sheet: function[5:0] = INSTRUCTION[5:0];
  //   immediate[15:0] = INSTRUCTION[15:0]; word_addressed_target[23:0] = INSTRUCTION[23:0];
  //   shift_amount[4:0] = INSTRUCTION[10:6]; register_d[4:0] = INSTRUCTION[15:11];
  //   register_s[4:0] = INSTRUCTION[25:21]; opcode[5:0] = INSTRUCTION[31:26]

  // Notes on the sheet:
  //   These are outputs/inputs from run.circ
  //   These are outputs to run.circ
endmodule
